# Fritzing sketch Lancador (saved by Fritzing 0.9.3b)
breadboards: 1

parts:
  S1 = H-Bridge with L298N
  Componente1 = Arduino Mega 2560 (Rev3)
  M1 = DC Motor
  R1 = Resistor [tolerance=±5% resistance=220 package=THT]
  LED1 = LED - 5mm [color="Red (633nm)" package="5 mm [THT]"]
  LED2 = LED - 5mm [color="Red (633nm)" package="5 mm [THT]"]
  LED3 = LED - 5mm [color="Red (633nm)" package="5 mm [THT]"]
  S2 = Pushbutton [package="[THT]"]
  R2 = Resistor [tolerance=±5% resistance=220 package=THT]

nets:
  GND: S1.GND, Componente1.GND, R1.Pin_0
  N1: S1.IN3, Componente1.D24
  N2: S1.IN4, Componente1.D26
  N3: S1.M2-01, M1.pin_2
  N4: S1.M2-02, M1.pin_1
  N5: Componente1.D9_PWM, R2.Pin_0
  N6: Componente1.5V, S2.Pin_1, S2.Pin_2
  N7: Componente1.D2_PWM, LED3.anode
  N8: Componente1.D5_PWM, LED2.anode
  N9: Componente1.D7_PWM, LED1.anode
  N10: R1.Pin_1, LED1.cathode, LED2.cathode, LED3.cathode
  N11: S2.Pin_3, R2.Pin_1

custom parts:
  H-Bridge with L298N: h-bridge
